# Fritzing sketch Milestone Pico Pinout (saved by Fritzing 0.9.10b)
breadboards: 1

parts:
  Pico_H1 = Raspberry Pi Pico H
  U1 = Nokia 6100 Color LCD [package=nokia6100_lcd]  # not connected
  M1 = Dagu DGServo 9g (Top view) [part_number=RS001B]
  M2 = Dagu DGServo 9g (Top view) [part_number=RS001B]
  M3 = Dagu DGServo 9g (Top view) [part_number=RS001B]
  M4 = Dagu DGServo 9g (Top view) [part_number=RS001B]

nets:
  N1: Pico_H1.GP21, M1.pulse
  N2: Pico_H1.GP20, M2.pulse
  N3: Pico_H1.GP19, M3.pulse
  N4: Pico_H1.GP18, M4.pulse
  GND: M1.gnd, M2.gnd, M3.gnd, M4.gnd
  VCC: M1.vcc, M2.vcc, M3.vcc, M4.vcc

notes:
  Servo:
  - Left foot lower: GP21
  - Right foot lower: GP20
  - Left foot upper: GP19
  - Right foot upper: GP18
  LCD:
  - DC (Data command): GP8
  - CS (chip select): GP9
  - CLK (SPI clock): GP10
  - DIN (Master out, slave in): GP11
  - RST (Active low reset): GP12
  - BL (backlight): GP13
  Example display, not the actual model we are using (need to find the model and import to Fritizing)

custom parts:
  Raspberry Pi Pico H: Raspberry Pi Pico H. Based around the RP2040 microcontroller the Pico H is a low cost microcontroller device bringing Raspberry Pi quality, cost, and easy of use to the microcontroller space.
